// Logisim project MIPS - Single cycle.circ as structural Verilog: 4 circuits, main circuit main
module main (
);

  wire button_1_out, CLK;
  wire [2:0] funct;
  wire [7:3] Immediate;
  wire [15:0] PC;
  wire [15:8] Insrtuction;

  Clock clock_1 (.out(CLK));
  PC pc_1 (.Data__Instruction_Address(PC), .CLK(CLK), .Reset(button_1_out));  // open: Next_Address
  Button button_1 (.out(button_1_out));
  Instruction_Memory instruction_memory_1 (.Address(PC), .Data__Instruction({Insrtuction, Immediate, funct}));

  // Other names for the same wires on the sheet: Immediate[2:0] = funct; Insrtuction[7:0] = {Immediate, funct};
  //   Jump_Address[11:0] = {Insrtuction[11:8], Immediate, funct}; OP_CODE[3:0] = Insrtuction[15:12];
  //   Rd[1:0] = Immediate[7:6]; Rs[1:0] = Insrtuction[11:10]; Rt[1:0] = Insrtuction[9:8];
  //   tunnel[2:0] = Immediate[5:3]

  // Notes on the sheet:
  //   J-Type
  //   I-Type
endmodule

module Control_Unit (
  input  [3:0] OP_CODE,
  output Register_Destination,
  output ALU_Source,
  output Memory_To_Register,
  output Register_Write,
  output Memory_Read,
  output Memory_Write,
  output Branch_Equal,
  output Branch_Not_Equal,
  output Jump,
  output ALU_OP_1,
  output ALU_OP_0
);

  wire addi_out, andi_out, lui_out, not_1_out, not_2_out, not_3_out, not_4_out, not_5_out, not_6_out,
       not_7_out, not_8_out, not_9_out, not_10_out, not_11_out, not_12_out, not_13_out, not_14_out,
       not_15_out, not_16_out, not_17_out, not_18_out, not_19_out, not_20_out, not_21_out, not_22_out,
       not_23_out, not_24_out, ori_out, sw_out;

  not not_1 (not_1_out, OP_CODE[1]);
  not not_2 (not_2_out, OP_CODE[2]);
  not not_3 (not_3_out, OP_CODE[0]);
  not not_4 (not_4_out, OP_CODE[3]);
  and R_fomat (ALU_OP_1, not_4_out, not_2_out, not_1_out, not_3_out);
  not not_5 (not_5_out, OP_CODE[2]);
  not not_6 (not_6_out, OP_CODE[3]);
  not not_7 (not_7_out, OP_CODE[0]);
  and lui (lui_out, not_6_out, not_5_out, OP_CODE[1], not_7_out);
  not not_8 (not_8_out, OP_CODE[2]);
  not not_9 (not_9_out, OP_CODE[3]);
  not not_10 (not_10_out, OP_CODE[3]);
  and ori (ori_out, not_9_out, not_8_out, OP_CODE[1], OP_CODE[0]);
  not not_11 (not_11_out, OP_CODE[0]);
  not not_12 (not_12_out, OP_CODE[1]);
  not not_13 (not_13_out, OP_CODE[3]);
  and addi (addi_out, not_10_out, OP_CODE[2], not_12_out, not_11_out);
  not not_14 (not_14_out, OP_CODE[3]);
  not not_15 (not_15_out, OP_CODE[1]);
  and andi (andi_out, not_13_out, OP_CODE[2], not_15_out, OP_CODE[0]);
  and lw (Memory_To_Register, not_14_out, OP_CODE[2], OP_CODE[1], not_17_out);
  not not_16 (not_16_out, OP_CODE[3]);
  not not_17 (not_17_out, OP_CODE[0]);
  and sw (sw_out, not_16_out, OP_CODE[2], OP_CODE[1], OP_CODE[0]);
  not not_18 (not_18_out, OP_CODE[0]);
  not not_19 (not_19_out, OP_CODE[2]);
  not not_20 (not_20_out, OP_CODE[1]);
  and u_jump (Jump, OP_CODE[3], not_19_out, not_20_out, not_18_out);
  not not_21 (not_21_out, OP_CODE[1]);
  not not_22 (not_22_out, OP_CODE[2]);
  and beq (Branch_Equal, OP_CODE[3], not_22_out, not_21_out, OP_CODE[0]);
  not not_23 (not_23_out, OP_CODE[0]);
  not not_24 (not_24_out, OP_CODE[2]);
  and bne (Branch_Not_Equal, OP_CODE[3], not_24_out, OP_CODE[1], not_23_out);
  or or_1 (ALU_Source, lui_out, ori_out, addi_out, andi_out, Memory_To_Register, sw_out);
  or or_2 (Register_Write, ALU_OP_1, lui_out);
  // OR_Gate or_3 has open pins: out=Memory_Read
  // OR_Gate or_4 has open pins: out=Memory_Write
  or or_5 (ALU_OP_0, Branch_Equal, Branch_Not_Equal);

  assign Register_Destination = ALU_OP_1;
endmodule

module Instruction_Memory (
  input  [15:0] Address,
  output [15:0] Data__Instruction
);

  ROM #(.addrWidth(16), .dataWidth(16)) rom_1 (.addr(Address), .data(Data__Instruction));  // open: sel

  // Notes on the sheet:
  //   Instruction Memory
endmodule

module PC (
  input  [15:0] Next_Address,
  input  CLK,
  input  Reset,
  output [15:0] Data__Instruction_Address
);

  Register #(.width(16)) PC (.D(Next_Address), .Q(Data__Instruction_Address), .clk(CLK), .clr(Reset));  // open: en
endmodule
